// Logisim project Booth_algo.circ as structural Verilog: 1 circuit, main circuit main
module main (
  input  [3:0] in_1,
  input  [3:0] M,
  input  [3:0] Q,
  input  [1:0] in_4,
  input  [1:0] in_5,
  input  [1:0] in_6,
  input  [1:0] in_7,
  input  [1:0] in_8,
  input  [1:0] in_9,
  input  [1:0] in_10,
  input  [1:0] in_11,
  output [7:0] out_12
);

  wire comparator_1_eq, comparator_1_gt, comparator_1_lt, comparator_2_eq, comparator_2_gt, comparator_2_lt,
       comparator_3_eq, comparator_3_gt, comparator_3_lt, comparator_4_eq, comparator_4_gt, comparator_4_lt;
  wire [2:0] and_1_out, and_4_out, and_7_out, and_10_out;
  wire [3:0] adder_5_out, adder_6_out, adder_7_out, bit_extender_1_out, bit_extender_2_out,
       bit_extender_3_out, bit_extender_4_out, multiplexer_1_out, multiplexer_2_out, multiplexer_3_out,
       multiplexer_4_out, negator_1_out, shifter_1_out, shifter_2_out, shifter_3_out, shifter_4_out,
       shifter_5_out, shifter_6_out, shifter_7_out, shifter_8_out;
  wire [3:1] adder_1_out, adder_2_out, adder_3_out, adder_4_out;

  // Probe on Q
  // Probe on M
  Comparator #(.width(1)) comparator_1 (
    .a(Q[0]), .b(1'b0), .gt(comparator_1_gt), .eq(comparator_1_eq), .lt(comparator_1_lt));
  Comparator #(.width(1)) comparator_2 (
    .a(Q[1]), .b(Q[0]), .gt(comparator_2_gt), .eq(comparator_2_eq), .lt(comparator_2_lt));
  Comparator #(.width(1)) comparator_3 (
    .a(Q[2]), .b(Q[1]), .gt(comparator_3_gt), .eq(comparator_3_eq), .lt(comparator_3_lt));
  Comparator #(.width(1)) comparator_4 (
    .a(Q[3]), .b(Q[2]), .gt(comparator_4_gt), .eq(comparator_4_eq), .lt(comparator_4_lt));
  Negator #(.width(4)) negator_1 (.in(M), .out(negator_1_out));
  and and_1 (and_1_out[0], comparator_1_gt, 1'b1);
  and and_2 (and_1_out[1], comparator_1_eq, 1'b1);
  and and_3 (and_1_out[2], comparator_1_lt, 1'b1);
  and and_4 (and_4_out[0], comparator_2_gt, 1'b1);
  and and_5 (and_4_out[1], comparator_2_eq, 1'b1);
  and and_6 (and_4_out[2], comparator_2_lt, 1'b1);
  and and_7 (and_7_out[0], comparator_3_gt, 1'b1);
  and and_8 (and_7_out[1], comparator_3_eq, 1'b1);
  and and_9 (and_7_out[2], comparator_3_lt, 1'b1);
  and and_10 (and_10_out[0], comparator_4_gt, 1'b1);
  and and_11 (and_10_out[1], 1'b1, comparator_4_eq);
  and and_12 (and_10_out[2], comparator_4_lt, 1'b1);
  Multiplexer #(.select(3), .width(4)) multiplexer_1 (
    .in1(M), .in2(4'b0000), .in4(negator_1_out), .out(multiplexer_1_out), .sel(and_1_out));  // open: in0, in3, in5, in6, in7, en
  Multiplexer #(.select(3), .width(4)) multiplexer_2 (
    .in1(M), .in2(4'b0000), .in4(negator_1_out), .out(multiplexer_2_out), .sel(and_4_out));  // open: in0, in3, in5, in6, in7, en
  Multiplexer #(.select(3), .width(4)) multiplexer_3 (
    .in1(M), .in2(4'b0000), .in4(negator_1_out), .out(multiplexer_3_out), .sel(and_7_out));  // open: in0, in3, in5, in6, in7, en
  Multiplexer #(.select(3), .width(4)) multiplexer_4 (
    .in1(M), .in2(4'b0000), .in4(negator_1_out), .out(multiplexer_4_out), .sel(and_10_out));  // open: in0, in3, in5, in6, in7, en
  Adder #(.width(4)) adder_1 (.a(in_1), .b(multiplexer_1_out), .out({adder_1_out, out_12[0]}));  // open: cin, cout
  Adder #(.width(4)) adder_2 (
    .a(adder_5_out), .b(multiplexer_2_out), .out({adder_2_out, out_12[1]}));  // open: cin, cout
  Adder #(.width(4)) adder_3 (
    .a(adder_6_out), .b(multiplexer_3_out), .out({adder_3_out, out_12[2]}));  // open: cin, cout
  Adder #(.width(4)) adder_4 (
    .a(adder_7_out), .b(multiplexer_4_out), .out({adder_4_out, out_12[3]}));  // open: cin, cout
  Shifter #(.width(4), .shift("lr")) shifter_1 (.in({adder_1_out, out_12[0]}), .\dist (in_4), .out(shifter_1_out));
  Shifter #(.width(4), .shift("lr")) shifter_2 (.in({adder_2_out, out_12[1]}), .\dist (in_6), .out(shifter_2_out));
  Shifter #(.width(4), .shift("lr")) shifter_3 (.in({adder_3_out, out_12[2]}), .\dist (in_8), .out(shifter_3_out));
  Shifter #(.width(4), .shift("lr")) shifter_4 (.in({adder_4_out, out_12[3]}), .\dist (in_10), .out(shifter_4_out));
  assign bit_extender_1_out = {{3{1'b0}}, 1'b1};  // Bit_Extender bit_extender_1
  assign bit_extender_2_out = {{3{1'b0}}, 1'b1};  // Bit_Extender bit_extender_2
  assign bit_extender_3_out = {{3{1'b0}}, 1'b0};  // Bit_Extender bit_extender_3
  assign bit_extender_4_out = {{3{1'b0}}, 1'b0};  // Bit_Extender bit_extender_4
  Shifter #(.width(4)) shifter_5 (.in(bit_extender_1_out), .\dist (in_5), .out(shifter_5_out));
  Shifter #(.width(4)) shifter_6 (.in(bit_extender_2_out), .\dist (in_7), .out(shifter_6_out));
  Shifter #(.width(4)) shifter_7 (.in(bit_extender_3_out), .\dist (in_9), .out(shifter_7_out));
  Shifter #(.width(4)) shifter_8 (.in(bit_extender_4_out), .\dist (in_11), .out(shifter_8_out));
  Adder #(.width(4)) adder_5 (.a(shifter_1_out), .b(shifter_5_out), .out(adder_5_out));  // open: cin, cout
  Adder #(.width(4)) adder_6 (.a(shifter_2_out), .b(shifter_6_out), .out(adder_6_out));  // open: cin, cout
  Adder #(.width(4)) adder_7 (.a(shifter_3_out), .b(shifter_7_out), .out(adder_7_out));  // open: cin, cout
  Adder #(.width(4)) adder_8 (.a(shifter_4_out), .b(shifter_8_out), .out(out_12[7:4]));  // open: cin, cout
  // Probe on out_12

  // Notes on the sheet:
  //   MUltiplier
  //   Multiplicand
  //   IMPLEMENTATION OF BOOTH's ALGORITHM
endmodule
